# Fritzing sketch arduino_final (saved by Fritzing 0.9.0b)
breadboards: 1

parts:
  Part1 = Arduino Uno (Rev3)
  J2 = Piezo Speaker
  U1 = GP1A57HR [package=gp1a57hr]
  R2 = Resistor [tolerance=±5% resistance=220 package=THT]
  J3 = Basic Force Sensing Resistor (FSR) [package=THT]
  R3 = Resistor [tolerance=±5% resistance=220 package=THT]
  LED1 = LED - 5mm [color="Red (633nm)" package="5 mm [THT]"]
  R4 = Resistor [tolerance=±5% resistance=220 package=THT]

nets:
  N1: Part1.A0, Part1.GND, J2.pin1, U1.3, U1.5, R3.Pin_0, R4.Pin_1
  N2: Part1.D8, J2.pin2
  N3: Part1.D11_PWM/MOSI, LED1.anode
  N4: Part1.D2, U1.2
  N5: Part1.5V, U1.1, R2.Pin_1, J3.pin_0
  N6: U1.4, R2.Pin_0
  N7: J3.pin_1, R3.Pin_1
  N8: LED1.cathode, R4.Pin_0

notes:
  LED represents LED strip and/or a bunch of LEDs
